# Fritzing sketch stepper_motor (saved by Fritzing 0.9.2b)
breadboards: 1

parts:
  Part1 = Arduino Uno (Rev3)
  Part2 = EasyDriver_v44
  M1 = Stepper Motor - Bipolar
  VCC1 = Battery block 9V

nets:
  N1: Part1.D8, Part2.DIR
  N2: Part1.D9_PWM, Part2.STEP
  GND: Part1.GND, Part2.GND, VCC1.-
  N3: Part2.V+, VCC1.+
  N4: Part2.OUT2A, M1.A
  N5: Part2.OUT2B, M1.C
  N6: Part2.OUT1A, M1.B
  N7: Part2.OUT1B, M1.D

// code stored in the sketch: motor.ino
int rot_speed = 245;

void setup() {                
  pinMode(8, OUTPUT);     
  pinMode(9, OUTPUT);
  digitalWrite(8, LOW);
  digitalWrite(9, LOW);
}

void loop() {
  digitalWrite(9, HIGH);
  delayMicroseconds(rot_speed);          
  digitalWrite(9, LOW); 
  delayMicroseconds(rot_speed);          
}
